# Fritzing sketch Solar Charging Station-MM (saved by Fritzing 0.9.3b)
circuit board: 3.1cm x 3.4cm
breadboards: 1

parts:
  solar = SO08 [chip_label=CN3083 package=SO]
  3_6k = Resistor [tolerance=±5% resistance=3.6k package="0805 [SMD]"]
  4_7u = Ceramic Capacitor [capacitance=4.7µF package="100 mil [THT, multilayer]"]
  Bat = Header 2 [package=jst-2-smd]
  Vout = female pin header, 2 pins [form="♀ (female)"]
  LED1 = smd LED [color="Red (633nm)" package="0603 [SMD]"]
  LED2 = smd LED [color="Green (555nm)" package="0603 [SMD]"]
  ss14 = Rectifier Diode [package="Melf DO-213 AA [SMD]"]
  Vin = female pin header, 2 pins [form="♀ (female)"]
  22µF = Ceramic Capacitor [capacitance=22µF package="0805 [SMD, multilayer]"]
  330 = Resistor [tolerance=±5% resistance=330 package="0805 [SMD]"]

nets:
  GND: solar.Temp, solar.GND, 3_6k.Pin_0, 4_7u.1, Bat.2, Vout.pin2, Vin.pin1, 22µF.1
  N1: solar.ISET, 3_6k.Pin_1
  N2: solar.VIN, ss14.cathode, 22µF.0, 330.Pin_1
  N3: solar.BAT, solar.FB, 4_7u.0, Bat.1, Vout.pin1
  N4: solar.CH, LED2.cathode
  N5: solar.OK, LED1.cathode
  N6: LED1.anode, LED2.anode, 330.Pin_0
  N7: ss14.anode, Vin.pin2

notes:
  Rage Industries
