# Fritzing sketch esp32-wroom-MM (saved by Fritzing 0.9.3b)
circuit board: 6.00255cm x 4.91937cm
breadboards: 1

parts:
  Bat = female pin header, 2 pins [form="♀ (female)"]
  ESP33 = ESP-WROOM-32 [ESP-32S] Module [part_number=ESP-WROOM-32]
  I2C-2 = female pin header, 4 pins [form="♀ (female)"]
  4_7μF1 = Capacitor [package=0805]
  U2 = Voltage Regulator [part_number=AP7361C-33E-13 package=sot223]
  4_7k = Resistor [tolerance=±5% resistance=4.7k package="0805 [SMD]"]
  4_7k_2 = Resistor [tolerance=±5% resistance=4.7k package="0805 [SMD]"]
  Reset2 = Momentary Switch [package=ksa_sealed_tac_switch]
  10k = Resistor [tolerance=±5% resistance=10k package="0805 [SMD]"]
  Boot1 = Momentary Switch [package=ksa_sealed_tac_switch]
  Tx_Rx1 = female pin header, 4 pins [form="♀ (female)"]
  DHT11 = female pin header, 4 pins [form="♀ (female)"]
  4_7μF2 = Capacitor [package=0805]
  10k_2 = Resistor [tolerance=±5% resistance=10k package="0805 [SMD]"]
  S5 = female pin header, 3 pins [form="♀ (female)"]
  S6 = female pin header, 3 pins [form="♀ (female)"]
  S7 = female pin header, 3 pins [form="♀ (female)"]
  s3 = female pin header, 3 pins [form="♀ (female)"]
  S8 = female pin header, 3 pins [form="♀ (female)"]
  Photocell = female pin header, 2 pins [form="♀ (female)"]
  4_7k_3 = Resistor [tolerance=±5% resistance=4.7k package="0805 [SMD]"]
  LED = smd LED [color="Red (633nm)" package="0805 [SMD]"]
  I2C-1 = female pin header, 4 pins [form="♀ (female)"]

nets:
  N1: Bat.pin1, 4_7μF1.1, U2.IN
  N2: Bat.pin2, ESP33.GND#50, 4_7μF1.2, U2.GND, 4_7μF2.2, S5.pin3, S6.pin3, S7.pin3, s3.pin3, S8.pin3, LED.cathode
  N3: ESP33.3V3, I2C-2.pin3, U2.OUT, 4_7k.Pin_1, 4_7k_2.Pin_1, 10k.Pin_1, Tx_Rx1.pin3, DHT11.pin4, 4_7μF2.1, 10k_2.Pin_1, S5.pin2, S6.pin2, S7.pin2, s3.pin2, S8.pin2, Photocell.pin2, LED.anode, I2C-1.pin3
  N4: ESP33.SVN, S5.pin1
  N5: ESP33.IO34, S7.pin1
  N6: ESP33.IO35, S8.pin1
  N7: ESP33.IO32, s3.pin1
  N8: ESP33.IO33, S6.pin1
  N9: ESP33.IO25, Photocell.pin1, 4_7k_3.Pin_0
  N10: ESP33.GND#51, Tx_Rx1.pin4, DHT11.pin1
  N11: ESP33.SD0, 4_7k_2.Pin_0
  N12: ESP33.SD1, 4_7k.Pin_0
  N13: ESP33.IO0, 10k.Pin_0, Boot1.2
  N14: ESP33.IO4, DHT11.pin3, 10k_2.Pin_0
  N15: ESP33.RXD0, Tx_Rx1.pin1
  N16: ESP33.TXD0, Tx_Rx1.pin2
  N17: ESP33.CMD, I2C-2.pin4, Reset2.2, 4_7k_3.Pin_1, I2C-1.pin4
  N18: I2C-2.pin1, I2C-1.pin1
  N19: I2C-2.pin2, I2C-1.pin2
  N20: Reset2.3, Boot1.3

notes:
  Rage Industries

custom parts:
  ESP-WROOM-32 [ESP-32S] Module: Espressif ESP-WROOM-32 WiFi/Bluetooth LE microcontroller module also known as the Ai-Thinker ESP-32S module with similar formfactor. The ESP32 is a microcontroller chip with WiFi and BLE capabilities. The chip is developed by Espressif and is the successor to the popular ESP8266 WiFi module.
  Voltage Regulator: Voltage Regulator AP7361C voltage regulator. LDO 3.3V output. Mouser SKU : 621-AP7361C-33E-13.
